# Fritzing sketch mypcbdesign (saved by Fritzing 0.8.7b)
breadboards: 1

parts:
  R1 = Resistor [tolerance=±5% resistance=220 package=THT]
  Part1 = SRF05 Ultrasonic Rangefinder
  Part2 = Photon
  LED1 = LED - 5mm [color="Red (633nm)" package="5 mm [THT]"]
  J1 = Piezo Speaker

nets:
  N1: R1.Pin_0, Part2.D2
  N2: R1.Pin_1, LED1.anode
  VCC: Part1.VCC, Part2.VIN
  N3: Part1.Trig, Part2.D1
  N4: Part1.Echo, Part2.D5
  GND: Part1.GND, Part2.GND, J1.pin1
  N5: Part2.D0, J1.pin2
